# Fritzing sketch Wiring Diagram (saved by Fritzing 0.9.3b)
breadboards: 1

parts:
  R1 = Rotary Potentiometer (Large) [maximum_resistance=100kΩ package=THT]
  R2 = Rotary Potentiometer (Large) [maximum_resistance=100kΩ package=THT]
  R3 = Rotary Potentiometer (Large) [maximum_resistance=100kΩ package=THT]
  R4 = Rotary Potentiometer (Large) [maximum_resistance=100kΩ package=THT]
  J1 = Basic Servo
  S1 = Pushbutton [package="[THT]"]
  Part1 = Arduino Uno (Rev3)
  R5 = Resistor [tolerance=±5% resistance=10k package=THT]
  R6 = Resistor [tolerance=±5% resistance=220 package=THT]
  R8 = Resistor [tolerance=±5% resistance=10k package=THT]
  LED1 = LED - 5mm [color="White (4500K)" package="5 mm [THT]"]

nets:
  GND: R1.leg1, R2.leg1, R3.leg1, R4.leg1, J1.gnd, Part1.GND, R5.Pin_1, LED1.anode
  N1: R1.wiper, Part1.A1
  VCC: R1.leg2, R2.leg2, R3.leg2, R4.leg2, J1.vcc, S1.Pin_3, Part1.5V
  N2: R2.wiper, Part1.A4/SDA
  N3: R3.wiper, Part1.A3
  N4: R4.wiper, Part1.A2
  N5: J1.pulse, Part1.D12/MISO
  N6: S1.Pin_1, S1.Pin_2, Part1.D13/SCK, R5.Pin_0
  N7: Part1.D11_PWM/MOSI, R6.Pin_0
  N8: R6.Pin_1, R8.Pin_0
  N9: R8.Pin_1, LED1.cathode
